// Logisim project B23CS1052_ALU.circ as structural Verilog: 1 circuit, main circuit main
module main (
  input  [31:0] First_Operand,
  input  [31:0] Second_operand,
  input  [3:0] ALU_Control_3_0,
  output [31:0] ALU_result,
  output Zero
);

  wire [31:0] adder_1_out, and_1_out, multiplexer_1_out, or_1_out, subtractor_1_out;

  Adder #(.width(32)) adder_1 (.a(First_Operand), .b(Second_operand), .out(adder_1_out));  // open: cin, cout
  Subtractor #(.width(32)) subtractor_1 (
    .a(First_Operand), .b(Second_operand), .out(subtractor_1_out));  // open: bin, bout
  assign and_1_out = First_Operand & Second_operand;  // AND_Gate and_1, 32 bits wide
  assign or_1_out = First_Operand | Second_operand;  // OR_Gate or_1, 32 bits wide
  Comparator #(.width(32)) comparator_1 (.a(First_Operand), .b(Second_operand), .eq(Zero));  // open: gt, lt
  Multiplexer #(.width(32), .enable("false")) multiplexer_1 (
    .in0({32{1'b0}}), .in1(32'h1), .out(multiplexer_1_out), .sel(subtractor_1_out[31]));
  Multiplexer #(.select(4), .width(32), .enable("false")) multiplexer_2 (
    .in0(and_1_out), .in1(or_1_out), .in2(adder_1_out), .in6(subtractor_1_out), .in7(multiplexer_1_out),
    .out(ALU_result), .sel(ALU_Control_3_0));  // open: in3, in4, in5, in8, in9, in10, in11, in12, in13, in14, in15
endmodule
