// Logisim project B23CS1052_ALUSrc_Mux.circ as structural Verilog: 1 circuit, main circuit main
module main (
  input  [31:0] ReadData2,
  input  [31:0] signextended_immediate,
  input  ALUSrc,
  output [31:0] ALUSrc_Output
);

  Multiplexer #(.width(32), .enable("false")) multiplexer_1 (
    .in0(ReadData2), .in1(signextended_immediate), .out(ALUSrc_Output), .sel(ALUSrc));
endmodule
