// Logisim project B23CS1052_ALUcontrol.circ as structural Verilog: 1 circuit, main circuit main
module main (
  input  [3:0] addi,
  input  [3:0] beq,
  input  [1:0] ALU_op_1_0,
  input  [5:0] funct_code_5_0,
  input  [3:0] funct_code_3_0,
  input  [5:0] opcode,
  output [3:0] ALU_Control_3_0,
  output ALU_Control1,
  output [3:0] ALU_control_3_0__Rtype,
  output ALU_Control2,
  output [3:0] ALU_control_andi_ori,
  output ALU_Control0
);

  wire decoder_1_out0, decoder_1_out2, decoder_1_out5, decoder_1_out10, not_1_out, not_2_out, not_3_out,
       not_4_out;

  Multiplexer #(.select(2), .width(4), .enable("false")) multiplexer_1 (
    .in0(addi), .in1(beq), .in2({1'b0, ALU_Control2, ALU_Control1, ALU_Control0}),
    .in3({3'b000, ALU_control_andi_ori[0]}), .out(ALU_Control_3_0), .sel(ALU_op_1_0));
  Decoder #(.select(4), .enable("false")) decoder_1 (
    .out0(decoder_1_out0), .out2(decoder_1_out2), .out5(decoder_1_out5), .out10(decoder_1_out10),
    .sel(funct_code_3_0));  // open: out1, out3, out4, out6, out7, out8, out9, out11, out12, out13, out14, out15
  or or_1 (ALU_Control1, decoder_1_out0, decoder_1_out2, decoder_1_out10);
  or or_2 (ALU_Control0, decoder_1_out5, decoder_1_out10);
  or or_3 (ALU_Control2, decoder_1_out2, decoder_1_out10);
  not not_1 (not_1_out, opcode[0]);
  not not_2 (not_2_out, opcode[1]);
  not not_3 (not_3_out, opcode[4]);
  not not_4 (not_4_out, opcode[5]);
  // AND_Gate and_i_detect has open pins: in0=not_1_out, in1=not_2_out, in2=opcode[2], in3=opcode[3], in4=not_3_out, in5=not_4_out, out=open
  and or_i_detect (ALU_control_andi_ori[0], opcode[0], not_2_out, opcode[2], opcode[3], not_3_out, not_4_out);

  assign ALU_control_3_0__Rtype = {1'b0, ALU_Control2, ALU_Control1, ALU_Control0};
  assign ALU_control_andi_ori[3:1] = 3'b000;
  assign funct_code_5_0[3:0] = funct_code_3_0;
endmodule
