// Logisim project B23CS1052_BranchControl.circ as structural Verilog: 1 circuit, main circuit main
module main (
  input  Branch,
  input  Zero,
  output PCSrc
);

  and Branch_Control (PCSrc, Branch, Zero);
endmodule
