// Logisim project B23CS1052_Branch_Address_Calculation.circ as structural Verilog: 1 circuit, main circuit main
module main (
  input  [31:0] PC_4,
  input  [31:0] leftshifted_signextended_immedate,
  output [31:0] Branch_Target_Address
);

  Adder #(.width(32)) adder_1 (
    .a(PC_4), .b(leftshifted_signextended_immedate), .out(Branch_Target_Address));  // open: cin, cout
endmodule
