// Logisim project B23CS1052_ControlUnit.circ as structural Verilog: 1 circuit, main circuit main
module main (
  input  [5:0] opcode,
  output RegDst,
  output ALUSrc,
  output RegWrite,
  output Branch,
  output MemRead,
  output MemtoReg,
  output MemWrite,
  output [1:0] ALU_Op
);

  wire addi_out, andi_2_out, andi_3_out, andi_out, beq_2_out, not_1_out, not_2_out, not_3_out, not_4_out,
       not_5_out, not_6_out, not_7_out, not_8_out, not_9_out, not_10_out, not_11_out, not_12_out, not_13_out,
       not_14_out, not_15_out, not_16_out, not_17_out, not_18_out, not_19_out, not_20_out, not_21_out,
       not_22_out, not_23_out, not_24_out, not_25_out, not_26_out, not_27_out, not_28_out, not_29_out,
       not_30_out, not_31_out, not_32_out, not_33_out, not_34_out, not_35_out, not_36_out, not_37_out,
       not_38_out, not_39_out, ori_2_out, ori_3_out, ori_out, R_type_out;

  not not_1 (not_1_out, opcode[0]);
  not not_2 (not_2_out, opcode[1]);
  not not_3 (not_3_out, opcode[2]);
  not not_4 (not_4_out, opcode[3]);
  not not_5 (not_5_out, opcode[4]);
  not not_6 (not_6_out, opcode[5]);
  not not_7 (not_7_out, opcode[0]);
  not not_8 (not_8_out, opcode[1]);
  not not_9 (not_9_out, opcode[2]);
  not not_10 (not_10_out, opcode[2]);
  not not_11 (not_11_out, opcode[3]);
  not not_12 (not_12_out, opcode[4]);
  not not_13 (not_13_out, opcode[5]);
  not not_14 (not_14_out, opcode[3]);
  not not_15 (not_15_out, opcode[4]);
  not not_16 (not_16_out, opcode[4]);
  and R_type_opcode (RegDst, not_1_out, not_2_out, not_3_out, not_4_out, not_5_out, not_6_out);
  not not_17 (not_17_out, opcode[0]);
  not not_18 (not_18_out, opcode[1]);
  not not_19 (not_19_out, opcode[0]);
  not not_20 (not_20_out, opcode[1]);
  not not_21 (not_21_out, opcode[4]);
  not not_22 (not_22_out, opcode[5]);
  not not_23 (not_23_out, opcode[1]);
  and beq (Branch, not_7_out, not_8_out, opcode[2], not_11_out, not_12_out, not_13_out);
  and lw (MemRead, opcode[0], opcode[1], not_9_out, not_14_out, not_15_out, opcode[5]);
  and sw (MemWrite, opcode[0], opcode[1], not_10_out, opcode[3], not_16_out, opcode[5]);
  not not_24 (not_24_out, opcode[0]);
  not not_25 (not_25_out, opcode[2]);
  not not_26 (not_26_out, opcode[4]);
  not not_27 (not_27_out, opcode[5]);
  not not_28 (not_28_out, opcode[4]);
  not not_29 (not_29_out, opcode[5]);
  not not_30 (not_30_out, opcode[0]);
  not not_31 (not_31_out, opcode[1]);
  not not_32 (not_32_out, opcode[2]);
  not not_33 (not_33_out, opcode[3]);
  not not_34 (not_34_out, opcode[4]);
  not not_35 (not_35_out, opcode[5]);
  not not_36 (not_36_out, opcode[1]);
  not not_37 (not_37_out, opcode[4]);
  not not_38 (not_38_out, opcode[5]);
  and addi (addi_out, not_17_out, not_18_out, not_25_out, opcode[3], not_26_out, not_27_out);
  not not_39 (not_39_out, opcode[3]);
  and andi (andi_out, not_19_out, not_20_out, opcode[2], opcode[3], not_21_out, not_22_out);
  and ori (ori_out, opcode[0], not_23_out, opcode[2], opcode[3], not_28_out, not_29_out);
  and R_type (R_type_out, not_30_out, not_31_out, not_32_out, not_33_out, not_34_out, not_35_out);
  and andi_2 (andi_2_out, not_30_out, not_31_out, opcode[2], opcode[3], not_34_out, not_35_out);
  and ori_2 (ori_2_out, opcode[0], not_31_out, opcode[2], opcode[3], not_34_out, not_35_out);
  and andi_3 (andi_3_out, not_24_out, not_36_out, opcode[2], opcode[3], not_37_out, not_38_out);
  and ori_3 (ori_3_out, opcode[0], not_36_out, opcode[2], opcode[3], not_37_out, not_38_out);
  and beq_2 (beq_2_out, not_24_out, not_36_out, opcode[2], not_39_out, not_37_out, not_38_out);
  or or_1 (ALUSrc, addi_out, MemRead, andi_out, MemWrite, ori_out);
  or or_2 (RegWrite, addi_out, andi_out, MemRead, ori_out, RegDst);
  or or_3 (ALU_Op[1], R_type_out, andi_2_out, ori_2_out);
  or or_4 (ALU_Op[0], andi_3_out, ori_3_out, beq_2_out);

  assign MemtoReg = MemRead;
endmodule
