// Logisim project B23CS1052_DataMemory.circ as structural Verilog: 1 circuit, main circuit main
module main (
  input  [31:0] ALU_result,
  input  [31:0] Write_Data,
  input  MemRead,
  input  MemWrite,
  output [31:0] Ram_data_out
);

  wire clock_1_out, or_1_out;

  or or_1 (or_1_out, MemRead, MemWrite);
  Clock clock_1 (.out(clock_1_out));
  RAM #(.addrWidth(10), .dataWidth(32), .bus("separate")) ram_1 (
    .addr(ALU_result[11:2]), .din(Write_Data), .data(Ram_data_out), .sel(or_1_out), .clk(clock_1_out),
    .ld(MemRead), .clr(1'b0));  // open: str

  // Notes on the sheet:
  //   Data Memory
endmodule
