// Logisim project B23CS1052_InstructionMemory.circ as structural Verilog: 1 circuit, main circuit main
module main (
  input  [9:0] _10_bit_word_address,
  output [31:0] Instruction_fetched
);

  RAM #(.addrWidth(10), .dataWidth(32), .bus("asynch")) ram_1 (
    .addr(_10_bit_word_address), .data(Instruction_fetched), .sel(1'b1), .ld(1'b1), .clr(1'b0));

  // Notes on the sheet:
  //   Load ( setting it to zero makes the Instruction Memory Read only)
  //   chip select
  //   clear
  //   Instruction Memory
endmodule
