// Logisim project B23CS1052_LeftShiftby2.circ as structural Verilog: 1 circuit, main circuit main
module main (
  input  [31:0] signextended_immediate,
  output [31:0] signextended_immediate_after_leftshiftby2
);


  assign signextended_immediate_after_leftshiftby2 = {signextended_immediate[29:0], 2'b00};
endmodule
