// Logisim project B23CS1052_MemtoReg_Mux.circ as structural Verilog: 1 circuit, main circuit main
module main (
  input  [31:0] Read_Data,
  input  [31:0] ALU_Result,
  input  MemtoReg,
  output [31:0] Register_Write_Data
);

  Multiplexer #(.width(32), .enable("false")) multiplexer_1 (
    .in0(Read_Data), .in1(ALU_Result), .out(Register_Write_Data), .sel(MemtoReg));
endmodule
