// Logisim project B23CS1052_RegDst_Mux.circ as structural Verilog: 1 circuit, main circuit main
module main (
  input  [4:0] rt_20_16,
  input  [4:0] rd_11_15,
  input  RegDst,
  output [4:0] regdst_output
);

  Multiplexer #(.width(5), .enable("false")) multiplexer_1 (
    .in0(rt_20_16), .in1(rd_11_15), .out(regdst_output), .sel(RegDst));
endmodule
