// Logisim project B23CS1052_RegisterFile.circ as structural Verilog: 1 circuit, main circuit main
module main (
  input  [31:0] R0,
  input  [4:0] Write_Reg,
  input  [31:0] Write_Data,
  input  [4:0] Read_reg1,
  input  Reg_Write,
  input  [4:0] Read_reg2,
  output [31:0] Read_Data1,
  output [31:0] Read_Data2
);

  wire Clock_out, decoder_1_out1, decoder_1_out2, decoder_1_out3, decoder_1_out4, decoder_1_out5,
       decoder_1_out6, decoder_1_out7, decoder_1_out8, decoder_1_out9, decoder_1_out10, decoder_1_out11,
       decoder_1_out12, decoder_1_out13, decoder_1_out14, decoder_1_out15, decoder_1_out16, decoder_1_out17,
       decoder_1_out18, decoder_1_out19, decoder_1_out20, decoder_1_out21, decoder_1_out22, decoder_1_out23,
       decoder_1_out24, decoder_1_out25, decoder_1_out26, decoder_1_out27, decoder_1_out28, decoder_1_out29,
       decoder_1_out30, decoder_1_out31;
  wire [31:0] R1_q, R2_q, R3_q, R4_q, R5_q, R6_q, R7_q, R8_q, R9_q, R10_q, R11_q, R12_q, R13_q, R14_q, R15_q,
       R16_q, R17_q, R18_q, R19_q, R20_q, R21_q, R22_q, R23_q, R24_q, R25_q, R26_q, R27_q, R28_q, R29_q,
       R30_q, R31_q;

  Clock Clock (.out(Clock_out));
  Decoder #(.select(5)) decoder_1 (
    .out1(decoder_1_out1), .out2(decoder_1_out2), .out3(decoder_1_out3), .out4(decoder_1_out4),
    .out5(decoder_1_out5), .out6(decoder_1_out6), .out7(decoder_1_out7), .out8(decoder_1_out8),
    .out9(decoder_1_out9), .out10(decoder_1_out10), .out11(decoder_1_out11), .out12(decoder_1_out12),
    .out13(decoder_1_out13), .out14(decoder_1_out14), .out15(decoder_1_out15), .out16(decoder_1_out16),
    .out17(decoder_1_out17), .out18(decoder_1_out18), .out19(decoder_1_out19), .out20(decoder_1_out20),
    .out21(decoder_1_out21), .out22(decoder_1_out22), .out23(decoder_1_out23), .out24(decoder_1_out24),
    .out25(decoder_1_out25), .out26(decoder_1_out26), .out27(decoder_1_out27), .out28(decoder_1_out28),
    .out29(decoder_1_out29), .out30(decoder_1_out30), .out31(decoder_1_out31), .sel(Write_Reg), .en(Reg_Write));  // open: out0
  Register #(.width(32)) R8 (.D(Write_Data), .en(decoder_1_out8), .Q(R8_q), .clk(Clock_out));  // open: clr
  Register #(.width(32)) R16 (.D(Write_Data), .en(decoder_1_out16), .Q(R16_q), .clk(Clock_out));  // open: clr
  Register #(.width(32)) R24 (.D(Write_Data), .en(decoder_1_out24), .Q(R24_q), .clk(Clock_out));  // open: clr
  Register #(.width(32)) R1 (.D(Write_Data), .en(decoder_1_out1), .Q(R1_q), .clk(Clock_out));  // open: clr
  Register #(.width(32)) R9 (.D(Write_Data), .en(decoder_1_out9), .Q(R9_q), .clk(Clock_out));  // open: clr
  Register #(.width(32)) R17 (.D(Write_Data), .en(decoder_1_out17), .Q(R17_q), .clk(Clock_out));  // open: clr
  Register #(.width(32)) R25 (.D(Write_Data), .en(decoder_1_out25), .Q(R25_q), .clk(Clock_out));  // open: clr
  Register #(.width(32)) R2 (.D(Write_Data), .en(decoder_1_out2), .Q(R2_q), .clk(Clock_out));  // open: clr
  Register #(.width(32)) R10 (.D(Write_Data), .en(decoder_1_out10), .Q(R10_q), .clk(Clock_out));  // open: clr
  Register #(.width(32)) R18 (.D(Write_Data), .en(decoder_1_out18), .Q(R18_q), .clk(Clock_out));  // open: clr
  Register #(.width(32)) R26 (.D(Write_Data), .en(decoder_1_out26), .Q(R26_q), .clk(Clock_out));  // open: clr
  Register #(.width(32)) R3 (.D(Write_Data), .en(decoder_1_out3), .Q(R3_q), .clk(Clock_out));  // open: clr
  Register #(.width(32)) R11 (.D(Write_Data), .en(decoder_1_out11), .Q(R11_q), .clk(Clock_out));  // open: clr
  Register #(.width(32)) R19 (.D(Write_Data), .en(decoder_1_out19), .Q(R19_q), .clk(Clock_out));  // open: clr
  Register #(.width(32)) R4 (.D(Write_Data), .en(decoder_1_out4), .Q(R4_q), .clk(Clock_out));  // open: clr
  Register #(.width(32)) R12 (.D(Write_Data), .en(decoder_1_out12), .Q(R12_q), .clk(Clock_out));  // open: clr
  Register #(.width(32)) R27 (.D(Write_Data), .en(decoder_1_out27), .Q(R27_q), .clk(Clock_out));  // open: clr
  Register #(.width(32)) R20 (.D(Write_Data), .en(decoder_1_out20), .Q(R20_q), .clk(Clock_out));  // open: clr
  Register #(.width(32)) R28 (.D(Write_Data), .en(decoder_1_out28), .Q(R28_q), .clk(Clock_out));  // open: clr
  Register #(.width(32)) R5 (.D(Write_Data), .en(decoder_1_out5), .Q(R5_q), .clk(Clock_out));  // open: clr
  Register #(.width(32)) R13 (.D(Write_Data), .en(decoder_1_out13), .Q(R13_q), .clk(Clock_out));  // open: clr
  Register #(.width(32)) R21 (.D(Write_Data), .en(decoder_1_out21), .Q(R21_q), .clk(Clock_out));  // open: clr
  Register #(.width(32)) R6 (.D(Write_Data), .en(decoder_1_out6), .Q(R6_q), .clk(Clock_out));  // open: clr
  Register #(.width(32)) R14 (.D(Write_Data), .en(decoder_1_out14), .Q(R14_q), .clk(Clock_out));  // open: clr
  Register #(.width(32)) R29 (.D(Write_Data), .en(decoder_1_out29), .Q(R29_q), .clk(Clock_out));  // open: clr
  Register #(.width(32)) R22 (.D(Write_Data), .en(decoder_1_out22), .Q(R22_q), .clk(Clock_out));  // open: clr
  Register #(.width(32)) R30 (.D(Write_Data), .en(decoder_1_out30), .Q(R30_q), .clk(Clock_out));  // open: clr
  Register #(.width(32)) R7 (.D(Write_Data), .en(decoder_1_out7), .Q(R7_q), .clk(Clock_out));  // open: clr
  Register #(.width(32)) R15 (.D(R23_q), .en(decoder_1_out15), .Q(R15_q), .clk(Clock_out));  // open: clr
  Register #(.width(32)) R23 (.D(Write_Data), .en(decoder_1_out23), .Q(R23_q), .clk(Clock_out));  // open: clr
  Register #(.width(32)) R31 (.D(Write_Data), .en(decoder_1_out31), .Q(R31_q), .clk(Clock_out));  // open: clr
  Multiplexer #(.select(5), .width(32), .enable("false")) multiplexer_1 (
    .in0(R0), .in1(R1_q), .in2(R2_q), .in3(R3_q), .in4(R4_q), .in5(R5_q), .in6(R6_q), .in7(R7_q), .in8(R8_q),
    .in9(R9_q), .in10(R10_q), .in11(R11_q), .in12(R12_q), .in13(R13_q), .in14(R14_q), .in15(R15_q),
    .in16(R16_q), .in17(R17_q), .in18(R18_q), .in19(R19_q), .in20(R20_q), .in21(R21_q), .in22(R22_q),
    .in23(R23_q), .in24(R24_q), .in25(R25_q), .in26(R26_q), .in27(R27_q), .in28(R28_q), .in29(R29_q),
    .in30(R30_q), .in31(R31_q), .out(Read_Data2), .sel(Read_reg2));
  Multiplexer #(.select(5), .width(32), .enable("false")) multiplexer_2 (
    .in0(R0), .in1(R1_q), .in2(R2_q), .in3(R3_q), .in4(R4_q), .in5(R5_q), .in6(R6_q), .in7(R7_q), .in8(R8_q),
    .in9(R9_q), .in10(R10_q), .in11(R11_q), .in12(R12_q), .in13(R13_q), .in14(R14_q), .in15(R15_q),
    .in16(R16_q), .in17(R17_q), .in18(R18_q), .in19(R19_q), .in20(R20_q), .in21(R21_q), .in22(R22_q),
    .in23(R23_q), .in24(R24_q), .in25(R25_q), .in26(R26_q), .in27(R27_q), .in28(R28_q), .in29(R29_q),
    .in30(R30_q), .in31(R31_q), .out(Read_Data1), .sel(Read_reg1));
endmodule
