// Logisim project B23CS1052_SignExtend.circ as structural Verilog: 1 circuit, main circuit main
module main (
  input  [15:0] Immediate16,
  output [31:0] Signextended_immediate
);


  assign Signextended_immediate = {{17{Immediate16[15]}}, Immediate16[14:0]};
endmodule
