// Logisim project B23CS1052_main.circ as structural Verilog: 14 circuits, main circuit main
module main (
  output [31:0] out_1,
  output [4:0] out_2
);

  wire alu_1_zero, branchcontrol_1_pcsrc, clock_1_out, controlunit_1_alusrc, controlunit_1_branch,
       controlunit_1_memread, controlunit_1_memtoreg, controlunit_1_memwrite, controlunit_1_regdst,
       controlunit_1_regwrite, or_1_out;
  wire [1:0] controlunit_1_alu_op;
  wire [3:0] alucontrol_1_alu_control_3_0;
  wire [4:0] regdst_mux_1_regdst_output;
  wire [31:0] adder_1_out, adder_2_out, alusrc_mux_1_alusrc_output,
       leftshiftby2_1_signextended_immediate_after_leftshiftby2, memtoregmux_1_register_write_data,
       multiplexer_1_out, PC_q, ram_1_data, ram_2_data, registerfile_1_read_data1, registerfile_1_read_data2,
       signextend_1_signextended_immediate;

  Register #(.width(32)) PC (.D(multiplexer_1_out), .en(1'b1), .Q(PC_q), .clk(clock_1_out));  // open: clr
  Clock clock_1 (.out(clock_1_out));
  Adder #(.width(32)) adder_1 (.a(PC_q), .b(32'h4), .out(adder_1_out));  // open: cin, cout
  RAM #(.addrWidth(10), .dataWidth(32), .bus("asynch")) ram_1 (
    .addr(PC_q[11:2]), .data({ram_1_data[31:21], out_2, ram_1_data[15:0]}), .sel(1'b1), .ld(1'b1), .clr(1'b0));
  RegDst_Mux regdst_mux_1 (
    .rt_20_16(out_2), .regdst_output(regdst_mux_1_regdst_output), .rd_15_11(ram_1_data[15:11]),
    .RegDst(controlunit_1_regdst));
  ControlUnit controlunit_1 (
    .RegDst(controlunit_1_regdst), .ALUSrc(controlunit_1_alusrc), .opcode(ram_1_data[31:26]),
    .RegWrite(controlunit_1_regwrite), .Branch(controlunit_1_branch), .MemRead(controlunit_1_memread),
    .MemtoReg(controlunit_1_memtoreg), .MemWrite(controlunit_1_memwrite), .ALU_Op(controlunit_1_alu_op));
  SignExtend signextend_1 (
    .signextended_Immediate(signextend_1_signextended_immediate), .Immediate16(ram_1_data[15:0]));
  ALUControl alucontrol_1 (
    .ALU_Control_3_0(alucontrol_1_alu_control_3_0), .ALU_op_1_0(controlunit_1_alu_op),
    .funct_code_5_0(ram_1_data[5:0]), .opcode(ram_1_data[31:26]));
  RegisterFile registerfile_1 (
    .Write_Reg(regdst_mux_1_regdst_output), .Read_Data1(registerfile_1_read_data1),
    .Write_Data(memtoregmux_1_register_write_data), .Read_reg1(ram_1_data[25:21]),
    .RegWrite(controlunit_1_regwrite), .Read_Data2(registerfile_1_read_data2), .Read_reg2(out_2));
  LeftShiftby2 leftshiftby2_1 (
    .signextended_immediate_after_leftshiftby2(leftshiftby2_1_signextended_immediate_after_leftshiftby2),
    .signextended_immediate(signextend_1_signextended_immediate));
  ALUSrc_Mux alusrc_mux_1 (
    .ReadData2(registerfile_1_read_data2), .ALUSrc_Output(alusrc_mux_1_alusrc_output),
    .signextended_immediate(signextend_1_signextended_immediate), .ALUSrc(controlunit_1_alusrc));
  ALU alu_1 (
    .First_Operand(registerfile_1_read_data1), .Second_operand(alusrc_mux_1_alusrc_output),
    .ALU_result(out_1), .Zero(alu_1_zero), .ALU_Control_3_0(alucontrol_1_alu_control_3_0));
  Adder #(.width(32)) adder_2 (
    .a(adder_1_out), .b(leftshiftby2_1_signextended_immediate_after_leftshiftby2), .out(adder_2_out));  // open: cin, cout
  BranchControl branchcontrol_1 (.Branch(controlunit_1_branch), .PCSrc(branchcontrol_1_pcsrc), .Zero(alu_1_zero));
  or or_1 (or_1_out, controlunit_1_memread, controlunit_1_memwrite);
  Multiplexer #(.width(32), .enable("false")) multiplexer_1 (
    .in0(adder_1_out), .in1(adder_2_out), .out(multiplexer_1_out), .sel(branchcontrol_1_pcsrc));
  RAM #(.addrWidth(10), .dataWidth(32), .bus("separate")) ram_2 (
    .addr(out_1[11:2]), .din(registerfile_1_read_data2), .data(ram_2_data), .str(controlunit_1_memwrite),
    .sel(or_1_out), .clk(clock_1_out), .ld(controlunit_1_memread), .clr(1'b0));
  MemtoRegMux memtoregmux_1 (
    .Read_Data(out_1), .Register_Write_Data(memtoregmux_1_register_write_data), .ALU_Result(ram_2_data),
    .MemtoReg(controlunit_1_memtoreg));

  // Notes on the sheet:
  //   Instruction memory
  //   Instruction [15:0]
  //   Sign Extended Immediate
  //   PC+4
  //   PCSrc
  //   ALU Result
  //   Data Memory
endmodule

module ControlUnit (
  input  [5:0] opcode,
  output RegDst,
  output ALUSrc,
  output RegWrite,
  output Branch,
  output MemRead,
  output MemtoReg,
  output MemWrite,
  output [1:0] ALU_Op
);

  wire addi_out, andi_2_out, andi_3_out, andi_out, beq_2_out, not_1_out, not_2_out, not_3_out, not_4_out,
       not_5_out, not_6_out, not_7_out, not_8_out, not_9_out, not_10_out, not_11_out, not_12_out, not_13_out,
       not_14_out, not_15_out, not_16_out, not_17_out, not_18_out, not_19_out, not_20_out, not_21_out,
       not_22_out, not_23_out, not_24_out, not_25_out, not_26_out, not_27_out, not_28_out, not_29_out,
       not_30_out, not_31_out, not_32_out, not_33_out, not_34_out, not_35_out, not_36_out, not_37_out,
       not_38_out, not_39_out, ori_2_out, ori_3_out, ori_out, R_type_out;

  not not_1 (not_1_out, opcode[0]);
  not not_2 (not_2_out, opcode[1]);
  not not_3 (not_3_out, opcode[2]);
  not not_4 (not_4_out, opcode[3]);
  not not_5 (not_5_out, opcode[4]);
  not not_6 (not_6_out, opcode[5]);
  not not_7 (not_7_out, opcode[0]);
  not not_8 (not_8_out, opcode[1]);
  not not_9 (not_9_out, opcode[2]);
  not not_10 (not_10_out, opcode[2]);
  not not_11 (not_11_out, opcode[3]);
  not not_12 (not_12_out, opcode[4]);
  not not_13 (not_13_out, opcode[5]);
  not not_14 (not_14_out, opcode[3]);
  not not_15 (not_15_out, opcode[4]);
  not not_16 (not_16_out, opcode[4]);
  and R_type_opcode (RegDst, not_1_out, not_2_out, not_3_out, not_4_out, not_5_out, not_6_out);
  not not_17 (not_17_out, opcode[0]);
  not not_18 (not_18_out, opcode[1]);
  not not_19 (not_19_out, opcode[0]);
  not not_20 (not_20_out, opcode[1]);
  not not_21 (not_21_out, opcode[4]);
  not not_22 (not_22_out, opcode[5]);
  not not_23 (not_23_out, opcode[1]);
  and beq (Branch, not_7_out, not_8_out, opcode[2], not_11_out, not_12_out, not_13_out);
  and lw (MemRead, opcode[0], opcode[1], not_9_out, not_14_out, not_15_out, opcode[5]);
  and sw (MemWrite, opcode[0], opcode[1], not_10_out, opcode[3], not_16_out, opcode[5]);
  not not_24 (not_24_out, opcode[0]);
  not not_25 (not_25_out, opcode[2]);
  not not_26 (not_26_out, opcode[4]);
  not not_27 (not_27_out, opcode[5]);
  not not_28 (not_28_out, opcode[4]);
  not not_29 (not_29_out, opcode[5]);
  not not_30 (not_30_out, opcode[0]);
  not not_31 (not_31_out, opcode[1]);
  not not_32 (not_32_out, opcode[2]);
  not not_33 (not_33_out, opcode[3]);
  not not_34 (not_34_out, opcode[4]);
  not not_35 (not_35_out, opcode[5]);
  not not_36 (not_36_out, opcode[1]);
  not not_37 (not_37_out, opcode[4]);
  not not_38 (not_38_out, opcode[5]);
  and addi (addi_out, not_17_out, not_18_out, not_25_out, opcode[3], not_26_out, not_27_out);
  not not_39 (not_39_out, opcode[3]);
  and andi (andi_out, not_19_out, not_20_out, opcode[2], opcode[3], not_21_out, not_22_out);
  and ori (ori_out, opcode[0], not_23_out, opcode[2], opcode[3], not_28_out, not_29_out);
  and R_type (R_type_out, not_30_out, not_31_out, not_32_out, not_33_out, not_34_out, not_35_out);
  and andi_2 (andi_2_out, not_30_out, not_31_out, opcode[2], opcode[3], not_34_out, not_35_out);
  and ori_2 (ori_2_out, opcode[0], not_31_out, opcode[2], opcode[3], not_34_out, not_35_out);
  and andi_3 (andi_3_out, not_24_out, not_36_out, opcode[2], opcode[3], not_37_out, not_38_out);
  and ori_3 (ori_3_out, opcode[0], not_36_out, opcode[2], opcode[3], not_37_out, not_38_out);
  and beq_2 (beq_2_out, not_24_out, not_36_out, opcode[2], not_39_out, not_37_out, not_38_out);
  or or_1 (ALUSrc, addi_out, MemRead, andi_out, MemWrite, ori_out);
  or or_2 (RegWrite, addi_out, andi_out, MemRead, ori_out, RegDst);
  or or_3 (ALU_Op[1], R_type_out, andi_2_out, ori_2_out);
  or or_4 (ALU_Op[0], andi_3_out, ori_3_out, beq_2_out);

  assign MemtoReg = MemRead;
endmodule

module RegisterFile (
  input  [4:0] Write_Reg,
  input  [31:0] Write_Data,
  input  [4:0] Read_reg1,
  input  RegWrite,
  input  [4:0] Read_reg2,
  output [31:0] Read_Data1,
  output [31:0] Read_Data2
);

  wire Clock_out, decoder_1_out1, decoder_1_out2, decoder_1_out3, decoder_1_out4, decoder_1_out5,
       decoder_1_out6, decoder_1_out7, decoder_1_out8, decoder_1_out9, decoder_1_out10, decoder_1_out11,
       decoder_1_out12, decoder_1_out13, decoder_1_out14, decoder_1_out15, decoder_1_out16, decoder_1_out17,
       decoder_1_out18, decoder_1_out19, decoder_1_out20, decoder_1_out21, decoder_1_out22, decoder_1_out23,
       decoder_1_out24, decoder_1_out25, decoder_1_out26, decoder_1_out27, decoder_1_out28, decoder_1_out29,
       decoder_1_out30, decoder_1_out31;
  wire [31:0] R1_q, R2_q, R3_q, R4_q, R5_q, R6_q, R7_q, R8_q, R9_q, R10_q, R11_q, R12_q, R13_q, R14_q, R15_q,
       R16_q, R17_q, R18_q, R19_q, R20_q, R21_q, R22_q, R23_q, R24_q, R25_q, R26_q, R27_q, R28_q, R29_q,
       R30_q, R31_q;

  Clock Clock (.out(Clock_out));
  Decoder #(.select(5)) decoder_1 (
    .out1(decoder_1_out1), .out2(decoder_1_out2), .out3(decoder_1_out3), .out4(decoder_1_out4),
    .out5(decoder_1_out5), .out6(decoder_1_out6), .out7(decoder_1_out7), .out8(decoder_1_out8),
    .out9(decoder_1_out9), .out10(decoder_1_out10), .out11(decoder_1_out11), .out12(decoder_1_out12),
    .out13(decoder_1_out13), .out14(decoder_1_out14), .out15(decoder_1_out15), .out16(decoder_1_out16),
    .out17(decoder_1_out17), .out18(decoder_1_out18), .out19(decoder_1_out19), .out20(decoder_1_out20),
    .out21(decoder_1_out21), .out22(decoder_1_out22), .out23(decoder_1_out23), .out24(decoder_1_out24),
    .out25(decoder_1_out25), .out26(decoder_1_out26), .out27(decoder_1_out27), .out28(decoder_1_out28),
    .out29(decoder_1_out29), .out30(decoder_1_out30), .out31(decoder_1_out31), .sel(Write_Reg), .en(RegWrite));  // open: out0
  Register #(.width(32)) R8 (.D(Write_Data), .en(decoder_1_out8), .Q(R8_q), .clk(Clock_out));  // open: clr
  Register #(.width(32)) R16 (.D(Write_Data), .en(decoder_1_out16), .Q(R16_q), .clk(Clock_out));  // open: clr
  Register #(.width(32)) R24 (.D(Write_Data), .en(decoder_1_out24), .Q(R24_q), .clk(Clock_out));  // open: clr
  Register #(.width(32)) R1 (.D(Write_Data), .en(decoder_1_out1), .Q(R1_q), .clk(Clock_out));  // open: clr
  Register #(.width(32)) R9 (.D(Write_Data), .en(decoder_1_out9), .Q(R9_q), .clk(Clock_out));  // open: clr
  Register #(.width(32)) R17 (.D(Write_Data), .en(decoder_1_out17), .Q(R17_q), .clk(Clock_out));  // open: clr
  Register #(.width(32)) R25 (.D(Write_Data), .en(decoder_1_out25), .Q(R25_q), .clk(Clock_out));  // open: clr
  Register #(.width(32)) R2 (.D(Write_Data), .en(decoder_1_out2), .Q(R2_q), .clk(Clock_out));  // open: clr
  Register #(.width(32)) R10 (.D(Write_Data), .en(decoder_1_out10), .Q(R10_q), .clk(Clock_out));  // open: clr
  Register #(.width(32)) R18 (.D(Write_Data), .en(decoder_1_out18), .Q(R18_q), .clk(Clock_out));  // open: clr
  Register #(.width(32)) R26 (.D(Write_Data), .en(decoder_1_out26), .Q(R26_q), .clk(Clock_out));  // open: clr
  Register #(.width(32)) R3 (.D(Write_Data), .en(decoder_1_out3), .Q(R3_q), .clk(Clock_out));  // open: clr
  Register #(.width(32)) R11 (.D(Write_Data), .en(decoder_1_out11), .Q(R11_q), .clk(Clock_out));  // open: clr
  Register #(.width(32)) R19 (.D(Write_Data), .en(decoder_1_out19), .Q(R19_q), .clk(Clock_out));  // open: clr
  Register #(.width(32)) R4 (.D(Write_Data), .en(decoder_1_out4), .Q(R4_q), .clk(Clock_out));  // open: clr
  Register #(.width(32)) R12 (.D(Write_Data), .en(decoder_1_out12), .Q(R12_q), .clk(Clock_out));  // open: clr
  Register #(.width(32)) R27 (.D(Write_Data), .en(decoder_1_out27), .Q(R27_q), .clk(Clock_out));  // open: clr
  Register #(.width(32)) R20 (.D(R16_q), .en(decoder_1_out20), .Q(R20_q), .clk(Clock_out));  // open: clr
  Register #(.width(32)) R28 (.D(R16_q), .en(decoder_1_out28), .Q(R28_q), .clk(Clock_out));  // open: clr
  Register #(.width(32)) R5 (.D(Write_Data), .en(decoder_1_out5), .Q(R5_q), .clk(Clock_out));  // open: clr
  Register #(.width(32)) R13 (.D(Write_Data), .en(decoder_1_out13), .Q(R13_q), .clk(Clock_out));  // open: clr
  Register #(.width(32)) R21 (.D(Write_Data), .en(decoder_1_out21), .Q(R21_q), .clk(Clock_out));  // open: clr
  Register #(.width(32)) R6 (.D(Write_Data), .en(decoder_1_out6), .Q(R6_q), .clk(Clock_out));  // open: clr
  Register #(.width(32)) R14 (.D(Write_Data), .en(decoder_1_out14), .Q(R14_q), .clk(Clock_out));  // open: clr
  Register #(.width(32)) R29 (.D(Write_Data), .en(decoder_1_out29), .Q(R29_q), .clk(Clock_out));  // open: clr
  Register #(.width(32)) R22 (.D(Write_Data), .en(decoder_1_out22), .Q(R22_q), .clk(Clock_out));  // open: clr
  Register #(.width(32)) R30 (.D(Write_Data), .en(decoder_1_out30), .Q(R30_q), .clk(Clock_out));  // open: clr
  Register #(.width(32)) R7 (.D(Write_Data), .en(decoder_1_out7), .Q(R7_q), .clk(Clock_out));  // open: clr
  Register #(.width(32)) R15 (.D(Write_Data), .en(decoder_1_out15), .Q(R15_q), .clk(Clock_out));  // open: clr
  Register #(.width(32)) R23 (.D(Write_Data), .en(decoder_1_out23), .Q(R23_q), .clk(Clock_out));  // open: clr
  Register #(.width(32)) R31 (.D(Write_Data), .en(decoder_1_out31), .Q(R31_q), .clk(Clock_out));  // open: clr
  Multiplexer #(.select(5), .width(32), .enable("false")) multiplexer_1 (
    .in0({32{1'b0}}), .in1(R1_q), .in2(R2_q), .in3(R3_q), .in4(R4_q), .in5(R5_q), .in6(R6_q), .in7(R7_q),
    .in8(R8_q), .in9(R9_q), .in10(R10_q), .in11(R11_q), .in12(R12_q), .in13(R13_q), .in14(R14_q),
    .in15(R15_q), .in16(R16_q), .in17(R17_q), .in18(R18_q), .in19(R19_q), .in20(R20_q), .in21(R21_q),
    .in22(R22_q), .in23(R23_q), .in24(R24_q), .in25(R25_q), .in26(R26_q), .in27(R27_q), .in28(R28_q),
    .in29(R29_q), .in30(R30_q), .in31(R31_q), .out(Read_Data2), .sel(Read_reg2));
  Multiplexer #(.select(5), .width(32), .enable("false")) multiplexer_2 (
    .in0({32{1'b0}}), .in1(R1_q), .in2(R2_q), .in3(R3_q), .in4(R4_q), .in5(R5_q), .in6(R6_q), .in7(R7_q),
    .in8(R8_q), .in9(R9_q), .in10(R10_q), .in11(R11_q), .in12(R12_q), .in13(R13_q), .in14(R14_q),
    .in15(R15_q), .in16(R16_q), .in17(R17_q), .in18(R18_q), .in19(R19_q), .in20(R20_q), .in21(R21_q),
    .in22(R22_q), .in23(R23_q), .in24(R24_q), .in25(R25_q), .in26(R26_q), .in27(R27_q), .in28(R28_q),
    .in29(R29_q), .in30(R30_q), .in31(R31_q), .out(Read_Data1), .sel(Read_reg1));
endmodule

module RegDst_Mux (
  input  [4:0] rt_20_16,
  input  [4:0] rd_15_11,
  input  RegDst,
  output [4:0] regdst_output
);

  Multiplexer #(.width(5), .enable("false")) multiplexer_1 (
    .in0(rt_20_16), .in1(rd_15_11), .out(regdst_output), .sel(RegDst));
endmodule

module ALU (
  input  [31:0] First_Operand,
  input  [31:0] Second_operand,
  input  [3:0] ALU_Control_3_0,
  output [31:0] ALU_result,
  output Zero
);

  wire [31:0] adder_1_out, and_1_out, multiplexer_1_out, or_1_out, subtractor_1_out;

  Adder #(.width(32)) adder_1 (.a(First_Operand), .b(Second_operand), .out(adder_1_out));  // open: cin, cout
  Subtractor #(.width(32)) subtractor_1 (
    .a(First_Operand), .b(Second_operand), .out(subtractor_1_out));  // open: bin, bout
  assign and_1_out = First_Operand & Second_operand;  // AND_Gate and_1, 32 bits wide
  assign or_1_out = First_Operand | Second_operand;  // OR_Gate or_1, 32 bits wide
  Comparator #(.width(32)) comparator_1 (.a(First_Operand), .b(Second_operand), .eq(Zero));  // open: gt, lt
  Multiplexer #(.width(32), .enable("false")) multiplexer_1 (
    .in0({32{1'b0}}), .in1(32'h1), .out(multiplexer_1_out), .sel(subtractor_1_out[31]));
  Multiplexer #(.select(4), .width(32), .enable("false")) multiplexer_2 (
    .in0(and_1_out), .in1(or_1_out), .in2(adder_1_out), .in6(subtractor_1_out), .in7(multiplexer_1_out),
    .out(ALU_result), .sel(ALU_Control_3_0));  // open: in3, in4, in5, in8, in9, in10, in11, in12, in13, in14, in15
endmodule

module ALUSrc_Mux (
  input  [31:0] ReadData2,
  input  [31:0] signextended_immediate,
  input  ALUSrc,
  output [31:0] ALUSrc_Output
);

  Multiplexer #(.width(32), .enable("false")) multiplexer_1 (
    .in0(ReadData2), .in1(signextended_immediate), .out(ALUSrc_Output), .sel(ALUSrc));
endmodule

module SignExtend (
  input  [15:0] Immediate16,
  output [31:0] signextended_Immediate
);


  assign signextended_Immediate = {{17{Immediate16[15]}}, Immediate16[14:0]};
endmodule

module ALUControl (
  input  [1:0] ALU_op_1_0,
  input  [5:0] funct_code_5_0,
  input  [5:0] opcode,
  output [3:0] ALU_Control_3_0
);

  wire decoder_1_out0, decoder_1_out2, decoder_1_out5, decoder_1_out10, not_1_out, not_2_out, not_3_out,
       not_4_out;
  wire [0:0] or_i_detect_out;
  wire [2:0] or_2_out;

  Multiplexer #(.select(2), .width(4), .enable("false")) multiplexer_1 (
    .in0(4'b0010), .in1(4'b0110), .in2({1'b0, or_2_out}), .in3({3'b000, or_i_detect_out[0]}),
    .out(ALU_Control_3_0), .sel(ALU_op_1_0));
  Decoder #(.select(4), .enable("false")) decoder_1 (
    .out0(decoder_1_out0), .out2(decoder_1_out2), .out5(decoder_1_out5), .out10(decoder_1_out10),
    .sel(funct_code_5_0[3:0]));  // open: out1, out3, out4, out6, out7, out8, out9, out11, out12, out13, out14, out15
  or or_1 (or_2_out[1], decoder_1_out0, decoder_1_out2, decoder_1_out10);
  or or_2 (or_2_out[0], decoder_1_out5, decoder_1_out10);
  or or_3 (or_2_out[2], decoder_1_out2, decoder_1_out10);
  not not_1 (not_1_out, opcode[0]);
  not not_2 (not_2_out, opcode[1]);
  not not_3 (not_3_out, opcode[4]);
  not not_4 (not_4_out, opcode[5]);
  // AND_Gate and_i_detect has open pins: in0=not_1_out, in1=not_2_out, in2=opcode[2], in3=opcode[3], in4=not_3_out, in5=not_4_out, out=open
  and or_i_detect (or_i_detect_out[0], opcode[0], not_2_out, opcode[2], opcode[3], not_3_out, not_4_out);
endmodule

module BranchControl (
  input  Branch,
  input  Zero,
  output PCSrc
);

  and Branch_Control (PCSrc, Branch, Zero);
endmodule

module Branch_Address_Calculation (
  input  [31:0] PC_4,
  input  [31:0] leftshifted_signextended_immedate,
  output [31:0] Branch_Target_Address
);

  Adder #(.width(32)) adder_1 (
    .a(PC_4), .b(leftshifted_signextended_immedate), .out(Branch_Target_Address));  // open: cin, cout
endmodule

module LeftShiftby2 (
  input  [31:0] signextended_immediate,
  output [31:0] signextended_immediate_after_leftshiftby2
);


  assign signextended_immediate_after_leftshiftby2 = {signextended_immediate[29:0], 2'b00};
endmodule

module Instruction_Memory (
  input  [9:0] _10_bit_word_address,
  output [31:0] Instruction_fetched
);

  RAM #(.addrWidth(10), .dataWidth(32), .bus("asynch")) ram_1 (
    .addr(_10_bit_word_address), .data(Instruction_fetched), .sel(1'b1), .ld(1'b1), .clr(1'b0));

  // Notes on the sheet:
  //   Load ( setting it to zero makes the Instruction Memory Read only)
  //   chip select
  //   clear
  //   Instruction Memory
endmodule

module DataMemory (
  input  [31:0] ALU_result,
  input  [31:0] Write_Data,
  input  MemRead,
  input  MemWrite,
  output [31:0] Ram_data_out
);

  wire clock_1_out, or_1_out;

  or or_1 (or_1_out, MemRead, MemWrite);
  Clock clock_1 (.out(clock_1_out));
  RAM #(.addrWidth(10), .dataWidth(32), .bus("separate")) ram_1 (
    .addr(ALU_result[11:2]), .din(Write_Data), .data(Ram_data_out), .sel(or_1_out), .clk(clock_1_out),
    .ld(MemRead), .clr(1'b0));  // open: str

  // Notes on the sheet:
  //   Data Memory
endmodule

module MemtoRegMux (
  input  [31:0] Read_Data,
  input  [31:0] ALU_Result,
  input  MemtoReg,
  output [31:0] Register_Write_Data
);

  Multiplexer #(.width(32), .enable("false")) multiplexer_1 (
    .in0(Read_Data), .in1(ALU_Result), .out(Register_Write_Data), .sel(MemtoReg));
endmodule
